// Logisim project main.circ as structural Verilog: 4 circuits, main circuit main
module main (
);

  wire btn_peaton_reset_1_out_6, button_1_out, button_2_out, clock_1_out, ctrl_auto_1_amarillo,
       ctrl_auto_1_rojo, ctrl_auto_1_verde, ctrl_peaton_1_rojo, ctrl_peaton_1_verde, j_k_ff_1_q, j_k_ff_1_qn,
       j_k_ff_2_q, j_k_ff_2_qn, j_k_ff_3_q, j_k_ff_3_qn, j_k_ff_4_q, j_k_ff_4_qn, not_1_out, not_2_out,
       or_1_out, or_2_out, or_3_out, or_4_out, or_5_out;

  Button button_1 (.out(button_1_out));
  not not_1 (not_1_out, button_1_out);
  Clock #(.highDuration(5), .lowDuration(5)) clock_1 (.out(clock_1_out));
  not not_2 (not_2_out, clock_1_out);
  J_K_Flip_Flop j_k_ff_1 (
    .J(not_1_out), .clk(not_2_out), .K(not_1_out), .Q(j_k_ff_1_q), .Qn(j_k_ff_1_qn),
    .reset(btn_peaton_reset_1_out_6));  // open: preset, en
  J_K_Flip_Flop j_k_ff_2 (
    .J(not_1_out), .clk(j_k_ff_1_qn), .K(not_1_out), .Q(j_k_ff_2_q), .Qn(j_k_ff_2_qn),
    .reset(btn_peaton_reset_1_out_6));  // open: preset, en
  J_K_Flip_Flop j_k_ff_3 (
    .J(not_1_out), .clk(j_k_ff_2_qn), .K(not_1_out), .Q(j_k_ff_3_q), .Qn(j_k_ff_3_qn),
    .reset(btn_peaton_reset_1_out_6));  // open: preset, en
  J_K_Flip_Flop j_k_ff_4 (
    .J(not_1_out), .clk(j_k_ff_3_qn), .K(not_1_out), .Q(j_k_ff_4_q), .Qn(j_k_ff_4_qn),
    .reset(btn_peaton_reset_1_out_6));  // open: preset, en
  Button button_2 (.out(button_2_out));
  _7_Segment_Display u_7_segment_display_1 ();  // open: g, f, a, b, e, d, c, dp
  Btn_Peaton___Reset btn_peaton_reset_1 (
    .A(j_k_ff_4_q), .B(j_k_ff_3_q), .C(j_k_ff_2_q), .D(j_k_ff_1_q), .Btn_Peaton(button_2_out),
    .out_6(btn_peaton_reset_1_out_6));
  Ctrl_AUTO ctrl_auto_1 (
    .A(j_k_ff_4_q), .B(j_k_ff_3_q), .C(j_k_ff_2_q), .D(j_k_ff_1_q), .ROJO(ctrl_auto_1_rojo),
    .AMARILLO(ctrl_auto_1_amarillo), .VERDE(ctrl_auto_1_verde));
  Ctrl_PEATON ctrl_peaton_1 (
    .A(j_k_ff_4_q), .B(j_k_ff_3_q), .C(j_k_ff_2_q), .D(j_k_ff_1_q), .Rojo(ctrl_peaton_1_rojo),
    .Verde(ctrl_peaton_1_verde));
  _7_Segment_Display u_7_segment_display_2 ();  // open: g, f, a, b, e, d, c, dp
  or or_1 (or_1_out, button_1_out, ctrl_auto_1_rojo);
  or or_2 (or_2_out, button_1_out, ctrl_auto_1_amarillo);
  or or_3 (or_3_out, button_1_out, ctrl_auto_1_verde);
  or or_4 (or_4_out, button_1_out, ctrl_peaton_1_rojo);
  or or_5 (or_5_out, button_1_out, ctrl_peaton_1_verde);
  LED led_1 (.in(or_1_out));
  LED led_2 (.in(or_2_out));
  LED led_3 (.in(or_3_out));
  LED led_4 (.in(or_4_out));
  LED led_5 (.in(or_5_out));

  // Notes on the sheet:
  //   INICIALIZACION
  //   D
  //   C
  //   B
  //   BOTON PEATON
  //   A
  //   AUTO
  //   PEATON
  //   ROJO
  //   VERDE
  //   ROJO
  //   AMARILLO
  //   VERDE
endmodule

module Ctrl_PEATON (
  input  A,
  input  B,
  input  C,
  input  D,
  output Rojo,
  output Verde
);

  wire and_1_out, and_2_out, and_3_out, and_4_out, clock_1_out, j_k_ff_1_qn, not_1_out, not_2_out, not_3_out,
       not_4_out, not_5_out, not_6_out, or_1_out;

  not not_1 (not_1_out, A);
  not not_2 (not_2_out, B);
  not not_3 (not_3_out, C);
  not not_4 (not_4_out, D);
  not not_5 (not_5_out, A);
  and and_1 (and_1_out, A, not_2_out, not_3_out, not_4_out);
  and and_2 (and_2_out, not_5_out, B, C, D);
  and and_3 (and_3_out, not_1_out, not_2_out);
  and and_4 (and_4_out, not_1_out, not_3_out, not_4_out);
  or or_1 (or_1_out, and_1_out, and_2_out);
  or or_2 (Rojo, and_3_out, and_4_out);
  Clock clock_1 (.out(clock_1_out));
  not not_6 (not_6_out, Rojo);
  J_K_Flip_Flop j_k_ff_1 (
    .J(or_1_out), .clk(clock_1_out), .K(or_1_out), .Qn(j_k_ff_1_qn));  // open: Q, preset, en, reset
  and and_5 (Verde, not_6_out, j_k_ff_1_qn);
endmodule

module Ctrl_AUTO (
  input  A,
  input  B,
  input  C,
  input  D,
  output ROJO,
  output AMARILLO,
  output VERDE
);

  wire and_1_out, and_2_out, and_3_out, not_1_out, not_2_out, not_3_out, not_4_out, not_5_out, not_6_out,
       not_7_out, not_8_out, or_1_out;

  not not_1 (not_1_out, A);
  not not_2 (not_2_out, B);
  and and_1 (and_1_out, not_1_out, not_2_out, C, D);
  not not_3 (not_3_out, A);
  not not_4 (not_4_out, B);
  not not_5 (not_5_out, C);
  not not_6 (not_6_out, A);
  not not_7 (not_7_out, B);
  not not_8 (not_8_out, D);
  or or_1 (or_1_out, A, B);
  and and_2 (and_2_out, not_3_out, not_4_out, not_5_out);
  and and_3 (and_3_out, not_6_out, not_7_out, not_8_out);
  buf or_2 (ROJO, or_1_out);  // OR_Gate
  buf or_3 (AMARILLO, and_1_out);  // OR_Gate
  or or_4 (VERDE, and_2_out, and_3_out);
endmodule

module Btn_Peaton___Reset (
  input  A,
  input  B,
  input  C,
  input  D,
  input  Btn_Peaton,
  output out_6
);

  wire and_1_out, and_2_out, d_ff_1_qn, not_1_out, not_2_out;

  not not_1 (not_1_out, B);
  not not_2 (not_2_out, C);
  and and_1 (and_1_out, A, not_1_out, not_2_out, D);
  and and_2 (and_2_out, Btn_Peaton, out_6);
  D_Flip_Flop d_ff_1 (
    .clk(and_1_out), .D(d_ff_1_qn), .Q(out_6), .Qn(d_ff_1_qn), .reset(and_2_out));  // open: preset, en
endmodule
